# Fritzing sketch sonar (saved by Fritzing 0.9.3b)
breadboards: 1

parts:
  LCD1 = LCD screen  # not connected
  Part1 = Arduino Uno (Rev3)
  IIC1 = IIC Convterter [package=converter]
  hc-sr1 = hc-sr04
  R1 = Resistor [tolerance=±5% resistance=220 package=THT]
  R2 = Resistor [tolerance=±5% resistance=220 package=THT]
  LED1 = LED - 5mm [color="Red (633nm)" package="5 mm [THT]"]
  LED2 = LED - 5mm [color="Red (633nm)" package="5 mm [THT]"]
  VCC1 = Battery  # not connected
  M2 = Stepper Motor - Unipolar  # not connected

nets:
  N1: Part1.A4/SDA, IIC1.SDA
  N2: Part1.A5/SCL, IIC1.SCL
  N3: Part1.D8, hc-sr1.Echo
  GND: Part1.GND, IIC1.GND, hc-sr1.GND, R1.Pin_1, R2.Pin_1
  N4: Part1.D2, LED2.anode
  N5: Part1.D3_PWM, LED1.anode
  N6: Part1.D7, hc-sr1.Trig
  5V: Part1.5V, hc-sr1.VCC
  VIN: Part1.VIN, IIC1.Vcc
  N7: R1.Pin_0, LED2.cathode
  N8: R2.Pin_0, LED1.cathode

custom parts:
  IIC Convterter: Parallel to IIC Converter for HD44780 family LCDs

// code stored in the sketch: TermometarLCD.ino
#include <Wire.h>  // Dolazi Arduino IDE
#include <LiquidCrystal_I2C.h> // Skida se sa neta

// varijable za senzor teperature
int DHpin = 8;
byte dat [5];
byte read_data () {
  byte data;
  for (int i = 0; i < 8; i ++) {
    if (digitalRead (DHpin) == LOW) {
      while (digitalRead (DHpin) == LOW); // wait for 50us
      delayMicroseconds (30); // determine the duration of the high level to determine the data is '0 'or '1'
      if (digitalRead (DHpin) == HIGH)
        data |= (1 << (7-i)); // high front and low in the post
      while (digitalRead (DHpin) == HIGH); // data '1 ', wait for the next one receiver
     }
  }
return data;
}

LiquidCrystal_I2C lcd(0x27, 2, 1, 0, 4, 5, 6, 7, 3, POSITIVE);  // Set the LCD I2C address
 
void start_test () {
  digitalWrite (DHpin, LOW); // bus down, send start signal
  delay (30); // delay greater than 18ms, so DHT11 start signal can be detected
 
  digitalWrite (DHpin, HIGH);
  delayMicroseconds (40); // Wait for DHT11 response
 
  pinMode (DHpin, INPUT);
  while (digitalRead (DHpin) == HIGH);
  delayMicroseconds (80); // DHT11 response, pulled the bus 80us
  if (digitalRead (DHpin) == LOW);
  delayMicroseconds (80); // DHT11 80us after the bus pulled to start sending data
 
  for (int i = 0; i < 4; i ++) // receive temperature and humidity data, the parity bit is not considered
    dat[i] = read_data ();
 
  pinMode (DHpin, OUTPUT);
  digitalWrite (DHpin, HIGH); // send data once after releasing the bus, wait for the host to open the next Start signal
}
 
void setup () {
  Serial.begin (9600);
  lcd.begin(20,2);
  pinMode (DHpin, OUTPUT);
  lcd.backlight();
}
 
void loop () {
  start_test ();
  Serial.print ("Current humdity =");
  Serial.print (dat [0], DEC); // display the humidity-bit integer;
  Serial.print ('.');
  Serial.print (dat [1], DEC); // display the humidity decimal places;
  Serial.println ('%');
  Serial.print ("Current temperature =");
  Serial.print (dat [2], DEC); // display the temperature of integer bits;
  Serial.print ('.');
  Serial.print (dat [3], DEC); // display the temperature of decimal places;
  Serial.println ('C');
  delay (5000);
  lcd.setCursor(0,0);
  lcd.print ("humdity = ");
  lcd.print (dat [0], DEC); // display the humidity-bit integer;
  lcd.print ('.');
  lcd.print (dat [1], DEC); // display the humidity decimal places;
  lcd.print ('%');
  lcd.setCursor(0,1);
  lcd.print ("temp = ");
  lcd.print (dat [2], DEC); // display the temperature of integer bits;
  lcd.print ('.');
  lcd.print (dat [3], DEC); // display the temperature of decimal places;
  lcd.print ('C');
  
}
