# Fritzing sketch temperature (saved by Fritzing 0.9.3b)

parts:
  IIC2 = IIC Convterter [package=converter]
  LCD1 = LCD screen  # not connected
  Part1 = Arduino Uno (Rev3)
  RHT1 = Humidity and Temperature Sensor RHT03

nets:
  GND: IIC2.GND, Part1.GND, RHT1.GND_2
  VCC: IIC2.Vcc, Part1.5V
  N1: IIC2.SDA, Part1.A4/SDA
  N2: IIC2.SCL, Part1.A5/SCL
  N3: Part1.D7, RHT1.Data-signal
  3V3: Part1.3V3, RHT1.Vcc

custom parts:
  IIC Convterter: Parallel to IIC Converter for HD44780 family LCDs
